// Logisim project Project_Circuit_NAND.circ as structural Verilog: 1 circuit, main circuit main
module main (
  input  A,
  input  B,
  input  C,
  input  D,
  input  E
);

  wire nand_1_out, nand_2_out, nand_3_out, nand_4_out, nand_5_out, nand_6_out, nand_7_out, nand_8_out,
       nand_9_out, nand_10_out, nand_11_out, nand_12_out, nand_13_out, nand_14_out, nand_15_out, nand_16_out,
       nand_17_out, nand_18_out, nand_19_out, nand_20_out, nand_21_out, nand_22_out, nand_23_out,
       nand_24_out, nand_25_out, nand_26_out, nand_27_out, nand_28_out, not_1_out, not_2_out, not_3_out,
       not_4_out, not_5_out, not_6_out, not_7_out, not_8_out, not_9_out, not_10_out, not_11_out, not_12_out,
       not_13_out, not_14_out;

  not not_1 (not_1_out, A);
  not not_2 (not_2_out, B);
  not not_3 (not_3_out, C);
  not not_4 (not_4_out, D);
  not not_5 (not_5_out, E);
  not not_6 (not_6_out, C);
  not not_7 (not_7_out, B);
  not not_8 (not_8_out, C);
  not not_9 (not_9_out, D);
  nand nand_1 (nand_1_out, not_3_out, not_4_out);
  nand nand_2 (nand_2_out, not_6_out, not_7_out);
  nand nand_3 (nand_3_out, not_8_out, not_9_out);
  not not_10 (not_10_out, E);
  not not_11 (not_11_out, E);
  not not_12 (not_12_out, D);
  not not_13 (not_13_out, A);
  nand nand_4 (nand_4_out, nand_1_out, not_10_out);
  nand nand_5 (nand_5_out, not_11_out, not_12_out);
  nand nand_6 (nand_6_out, not_4_out, B);
  nand nand_7 (nand_7_out, D, C);
  nand nand_8 (nand_8_out, not_3_out, E, B);
  nand nand_9 (nand_9_out, C, not_2_out);
  nand nand_10 (nand_10_out, not_1_out, not_2_out, D);
  nand nand_11 (nand_11_out, not_4_out, A);
  nand nand_12 (nand_12_out, B, C);
  nand nand_13 (nand_13_out, C, E);
  nand nand_14 (nand_14_out, not_3_out, D, E);
  nand nand_15 (nand_15_out, B, nand_3_out, not_5_out);
  nand nand_16 (nand_16_out, not_1_out, B, nand_4_out);
  nand nand_17 (nand_17_out, nand_6_out, nand_7_out);
  nand nand_18 (nand_18_out, nand_10_out, nand_11_out);
  nand nand_19 (nand_19_out, nand_12_out, nand_13_out);
  nand nand_20 (nand_20_out, A, not_5_out, nand_2_out);
  nand nand_21 (nand_21_out, not_13_out, nand_15_out);
  nand nand_22 (nand_22_out, A, not_2_out, nand_5_out);
  nand nand_23 (nand_23_out, not_5_out, nand_17_out);
  nand nand_24 (nand_24_out, not_5_out, nand_18_out);
  nand nand_25 (nand_25_out, not_4_out, nand_19_out);
  not not_14 (not_14_out, nand_20_out);
  nand nand_26 (nand_26_out, nand_16_out, nand_22_out);
  nand nand_27 (nand_27_out, nand_23_out, nand_8_out, nand_9_out);
  nand nand_28 (nand_28_out, nand_24_out, nand_25_out, nand_14_out);
  LED Q (.in(nand_21_out));
  LED R (.in(nand_26_out));
  LED S (.in(nand_27_out));
  LED T (.in(nand_28_out));
  LED U (.in(not_14_out));
endmodule
