// Logisim project Project_Circuit_NOR.circ as structural Verilog: 1 circuit, main circuit main
module main (
  input  A,
  input  B,
  input  C,
  input  D,
  input  E
);

  wire nor_1_out, nor_2_out, nor_3_out, nor_4_out, nor_5_out, nor_6_out, nor_7_out, nor_8_out, nor_9_out,
       nor_10_out, nor_11_out, nor_12_out, nor_13_out, nor_14_out, nor_15_out, nor_16_out, nor_17_out,
       nor_18_out, nor_19_out, nor_20_out, nor_21_out, nor_22_out, nor_23_out, nor_24_out, nor_25_out,
       nor_26_out, nor_27_out, nor_28_out, not_1_out, not_2_out, not_3_out, not_4_out, not_5_out, not_6_out,
       not_7_out, not_8_out, not_9_out, not_10_out, not_11_out, not_12_out, not_13_out, not_14_out,
       not_15_out, not_16_out, not_17_out, not_18_out, not_19_out, not_20_out, not_21_out, not_22_out,
       not_23_out, not_24_out, not_25_out, not_26_out, not_27_out, not_28_out, not_29_out, not_30_out,
       not_31_out, not_32_out, not_33_out, not_34_out, not_35_out, not_36_out, not_37_out, not_38_out,
       not_39_out, not_40_out;

  not not_1 (not_1_out, A);
  not not_2 (not_2_out, B);
  not not_3 (not_3_out, C);
  not not_4 (not_4_out, D);
  not not_5 (not_5_out, E);
  not not_6 (not_6_out, not_3_out);
  not not_7 (not_7_out, not_4_out);
  nor nor_1 (nor_1_out, not_6_out, not_7_out);
  not not_8 (not_8_out, not_1_out);
  not not_9 (not_9_out, not_2_out);
  not not_10 (not_10_out, D);
  not not_11 (not_11_out, not_4_out);
  not not_12 (not_12_out, A);
  not not_13 (not_13_out, B);
  not not_14 (not_14_out, C);
  not not_15 (not_15_out, C);
  not not_16 (not_16_out, E);
  not not_17 (not_17_out, not_3_out);
  not not_18 (not_18_out, D);
  not not_19 (not_19_out, E);
  not not_20 (not_20_out, B);
  not not_21 (not_21_out, not_5_out);
  nor nor_2 (nor_2_out, C, D);
  not not_22 (not_22_out, B);
  not not_23 (not_23_out, D);
  not not_24 (not_24_out, C);
  not not_25 (not_25_out, not_3_out);
  not not_26 (not_26_out, E);
  not not_27 (not_27_out, B);
  not not_28 (not_28_out, C);
  not not_29 (not_29_out, not_2_out);
  nor nor_3 (nor_3_out, C, B);
  not not_30 (not_30_out, not_1_out);
  not not_31 (not_31_out, B);
  nor nor_4 (nor_4_out, nor_1_out, E);
  nor nor_5 (nor_5_out, E, D);
  nor nor_6 (nor_6_out, not_4_out, not_22_out);
  nor nor_7 (nor_7_out, not_23_out, not_24_out);
  nor nor_8 (nor_8_out, not_25_out, not_26_out, not_27_out);
  nor nor_9 (nor_9_out, not_28_out, not_29_out);
  nor nor_10 (nor_10_out, not_8_out, not_9_out, not_10_out);
  nor nor_11 (nor_11_out, not_11_out, not_12_out);
  nor nor_12 (nor_12_out, not_13_out, not_14_out);
  nor nor_13 (nor_13_out, not_15_out, not_16_out);
  nor nor_14 (nor_14_out, not_17_out, not_18_out, not_19_out);
  not not_32 (not_32_out, A);
  not not_33 (not_33_out, not_5_out);
  nor nor_15 (nor_15_out, not_20_out, nor_2_out, not_21_out);
  not not_34 (not_34_out, not_5_out);
  nor nor_16 (nor_16_out, nor_6_out, nor_7_out);
  not not_35 (not_35_out, not_5_out);
  nor nor_17 (nor_17_out, nor_10_out, nor_11_out);
  not not_36 (not_36_out, not_4_out);
  nor nor_18 (nor_18_out, nor_12_out, nor_13_out);
  nor nor_19 (nor_19_out, not_32_out, not_33_out, nor_3_out);
  nor nor_20 (nor_20_out, A, nor_15_out);
  nor nor_21 (nor_21_out, not_30_out, not_31_out, nor_4_out);
  nor nor_22 (nor_22_out, A, not_2_out, nor_5_out);
  nor nor_23 (nor_23_out, not_34_out, nor_16_out);
  nor nor_24 (nor_24_out, not_35_out, nor_17_out);
  nor nor_25 (nor_25_out, not_36_out, nor_18_out);
  not not_37 (not_37_out, nor_20_out);
  not not_38 (not_38_out, nor_26_out);
  nor nor_26 (nor_26_out, nor_21_out, nor_22_out);
  nor nor_27 (nor_27_out, nor_23_out, nor_8_out, nor_9_out);
  not not_39 (not_39_out, nor_27_out);
  nor nor_28 (nor_28_out, nor_24_out, nor_25_out, nor_14_out);
  not not_40 (not_40_out, nor_28_out);
  LED Q (.in(not_37_out));
  LED R (.in(not_38_out));
  LED T (.in(not_40_out));
  LED S (.in(not_39_out));
  LED U (.in(nor_19_out));
endmodule
